# Fritzing sketch Sensor Setup (saved by Fritzing 0.7.12b)

parts:
  Arduino1 = Arduino Fio
  SONAR1 = Maxbotix MaxSonar Ultrasonic Sensor

nets:
  N1: Arduino1.A0, SONAR1.AN
  GND: Arduino1.GND, SONAR1.GND
  3V3: Arduino1.3V3, SONAR1.+5V

custom parts:
  Maxbotix MaxSonar Ultrasonic Sensor: Maxbotix MaxSonar Ultrasonic Sensor LV-EZ0, LV-EZ1, LV-EZ2, LV-EZ3, LV-EZ4
